// Logisim project d-MIPS_PROCCESOR.circ as structural Verilog
module REGISTER_FILE (
  input  [23:0] in_1,
  input  [2:0] RA,
  input  [2:0] SL,
  input  [2:0] RB,
  input  enable,
  input  clk,
  input  clear,
  output [23:0] BusA,
  output [23:0] BusB
);

  wire and_1_out, and_2_out, and_3_out, and_4_out, and_5_out, and_6_out, and_7_out, and_8_out,
       decoder_1_out0, decoder_1_out1, decoder_1_out2, decoder_1_out3, decoder_1_out4, decoder_1_out5,
       decoder_1_out6, decoder_1_out7;
  wire [23:0] R0_q, R1_q, R2_q, R3_q, R4_q, R5_q, R6_q, R7_q;

  Decoder #(.select(3), .enable("false")) decoder_1 (
    .out0(decoder_1_out0), .out1(decoder_1_out1), .out2(decoder_1_out2), .out3(decoder_1_out3),
    .out4(decoder_1_out4), .out5(decoder_1_out5), .out6(decoder_1_out6), .out7(decoder_1_out7), .sel(SL));
  and and_1 (and_1_out, decoder_1_out0, 1'b0);
  and and_2 (and_2_out, decoder_1_out1, enable);
  and and_3 (and_3_out, decoder_1_out2, enable);
  and and_4 (and_4_out, decoder_1_out3, enable);
  and and_5 (and_5_out, decoder_1_out4, enable);
  and and_6 (and_6_out, decoder_1_out5, enable);
  and and_7 (and_7_out, decoder_1_out6, enable);
  and and_8 (and_8_out, decoder_1_out7, enable);
  Register #(.width(24), .trigger("falling")) R0 (.D(in_1), .en(and_1_out), .Q(R0_q), .clk(clk), .clr(clear));
  Register #(.width(24), .trigger("falling")) R1 (.D(in_1), .en(and_2_out), .Q(R1_q), .clk(clk), .clr(clear));
  Register #(.width(24), .trigger("falling")) R2 (.D(in_1), .en(and_3_out), .Q(R2_q), .clk(clk), .clr(clear));
  Register #(.width(24), .trigger("falling")) R3 (.D(in_1), .en(and_4_out), .Q(R3_q), .clk(clk), .clr(clear));
  Register #(.width(24), .trigger("falling")) R4 (.D(in_1), .en(and_5_out), .Q(R4_q), .clk(clk), .clr(clear));
  Register #(.width(24), .trigger("falling")) R5 (.D(in_1), .en(and_6_out), .Q(R5_q), .clk(clk), .clr(clear));
  Register #(.width(24), .trigger("falling")) R6 (.D(in_1), .en(and_7_out), .Q(R6_q), .clk(clk), .clr(clear));
  Register #(.width(24), .trigger("falling")) R7 (.D(in_1), .en(and_8_out), .Q(R7_q), .clk(clk), .clr(clear));
  Multiplexer #(.select(3), .width(24), .enable("false")) multiplexer_1 (
    .in0(R0_q), .in1(R1_q), .in2(R2_q), .in3(R3_q), .in4(R4_q), .in5(R5_q), .in6(R6_q), .in7(R7_q),
    .out(BusA), .sel(RA));
  Multiplexer #(.select(3), .width(24), .enable("false")) multiplexer_2 (
    .in0(R0_q), .in1(R1_q), .in2(R2_q), .in3(R3_q), .in4(R4_q), .in5(R5_q), .in6(R6_q), .in7(R7_q),
    .out(BusB), .sel(RB));
endmodule

module PC (
  input  [9:0] IMM10,
  input  [16:0] IMM17,
  input  in_3,
  input  in_4,
  input  in_5,
  input  [23:0] Rs,
  input  [1:0] PCSrc,
  output [23:0] out_8,
  output [23:0] out_9,
  output [2:0] out_10
);

  wire [23:0] adder_1_out, adder_2_out, bit_extender_1_out, bit_extender_2_out, multiplexer_1_out;

  assign bit_extender_1_out = {{14{IMM10[9]}}, IMM10};  // Bit_Extender bit_extender_1
  assign bit_extender_2_out = {{7{IMM17[16]}}, IMM17};  // Bit_Extender bit_extender_2
  Adder #(.width(24)) adder_1 (.a(out_9), .b(bit_extender_1_out), .out(adder_1_out));  // open: cin, cout
  Adder #(.width(24)) adder_2 (.a(out_8), .b(bit_extender_2_out), .out(adder_2_out));  // open: cin, cout
  Multiplexer #(.select(2), .width(24)) multiplexer_1 (
    .in0(out_9), .in1(adder_1_out), .in2(adder_2_out), .in3(Rs), .out(multiplexer_1_out), .sel(PCSrc),
    .en(1'b1));
  Register #(.width(24)) R1 (.D(multiplexer_1_out), .en(in_3), .Q(out_8), .clk(in_4), .clr(in_5));
  Adder #(.width(24)) adder_3 (.a(out_8), .b(24'h1), .out(out_9));  // open: cin, cout

  assign out_10 = 3'b111;
endmodule

module DATA_PATH (
  input  in_1,
  input  in_2,
  output [23:0] out_3,
  output out_4,
  output out_5,
  output out_6
);

  wire clock_1_out, control_unit_1_alusrc, control_unit_1_alusrc2, control_unit_1_cmp, control_unit_1_memrd,
       control_unit_1_memwr, control_unit_1_regwr, control_unit_1_sf, control_unit_1_shl,
       control_unit_1_typesel, control_unit_1_wbdata, control_unit_1_writesel;
  wire [1:0] control_unit_1_alu_op, control_unit_1_pc_op, control_unit_1_regdst;
  wire [2:0] multiplexer_1_out, multiplexer_2_out, pc_1_out_10;
  wire [9:0] rom_1_data;
  wire [16:10] rom_1_data_2;
  wire [23:0] bit_extender_1_out, bit_extender_2_out, multiplexer_3_out, multiplexer_4_out,
       multiplexer_5_out, multiplexer_6_out, pc_1_out_8, pc_1_out_9, ram_1_data, register_file_1_busa,
       register_file_1_busb;
  wire [23:17] rom_1_data_3;

  Clock clock_1 (.out(clock_1_out));
  PC pc_1 (
    .in_3(in_1), .in_5(in_2), .in_4(clock_1_out), .IMM10(rom_1_data), .IMM17({rom_1_data_2, rom_1_data}),
    .Rs(register_file_1_busb), .PCSrc(control_unit_1_pc_op), .out_9(pc_1_out_9), .out_8(pc_1_out_8),
    .out_10(pc_1_out_10));
  ROM #(.addrWidth(24), .dataWidth(24)) rom_1 (
    .addr(pc_1_out_8), .data({rom_1_data_3, rom_1_data_2, rom_1_data}), .sel(1'b1));
  Multiplexer #(.select(2), .width(3)) multiplexer_1 (
    .in0(rom_1_data_2[15:13]), .in1(pc_1_out_10), .in2(3'b001), .out(multiplexer_1_out),
    .sel(control_unit_1_regdst), .en(1'b1));  // open: in3
  Control_Unit control_unit_1 (
    .Instruction({rom_1_data_3, rom_1_data_2, rom_1_data}), .RegDst(control_unit_1_regdst),
    .WriteSel(control_unit_1_writesel), .ALUSrc(control_unit_1_alusrc), .ALU_Op(control_unit_1_alu_op),
    .MemWr(control_unit_1_memwr), .MemRd(control_unit_1_memrd), .RegWr(control_unit_1_regwr),
    .WBData(control_unit_1_wbdata), .SF(control_unit_1_sf), .TypeSel(control_unit_1_typesel), .ZF(out_4),
    .CLK(clock_1_out), .PC_OP(control_unit_1_pc_op), .ALUSrc2(control_unit_1_alusrc2),
    .SHL(control_unit_1_shl), .EQ(out_5), .CMP(control_unit_1_cmp));
  Multiplexer #(.width(3)) multiplexer_2 (
    .in0(rom_1_data[9:7]), .in1(multiplexer_1_out), .out(multiplexer_2_out), .sel(control_unit_1_typesel),
    .en(1'b1));
  Multiplexer #(.width(24)) multiplexer_3 (
    .in0(multiplexer_6_out), .in1(pc_1_out_9), .out(multiplexer_3_out), .sel(control_unit_1_writesel),
    .en(1'b1));
  assign bit_extender_1_out = {{7{rom_1_data_2[16]}}, {rom_1_data_2, rom_1_data}};  // Bit_Extender bit_extender_1
  assign bit_extender_2_out = {{14{rom_1_data[9]}}, rom_1_data};  // Bit_Extender bit_extender_2
  REGISTER_FILE register_file_1 (
    .in_1(multiplexer_3_out), .BusA(register_file_1_busa), .BusB(register_file_1_busb),
    .SL(multiplexer_1_out), .enable(control_unit_1_regwr), .RA(rom_1_data_2[12:10]), .RB(multiplexer_2_out),
    .clk(clock_1_out), .clear(in_2));
  Multiplexer #(.width(24)) multiplexer_4 (
    .in0(bit_extender_2_out), .in1(bit_extender_1_out), .out(multiplexer_4_out),
    .sel(control_unit_1_alusrc2), .en(1'b1));
  ALU alu_1 (
    .In_1(register_file_1_busa), .In_2(multiplexer_5_out), .ALU_OP(control_unit_1_alu_op),
    .SF(control_unit_1_sf), .Output(out_3), .EQ(out_5), .Zero_Flag(out_4), .GT(out_6),
    .Shift_CAS(control_unit_1_shl), .CMP(control_unit_1_cmp));
  Multiplexer #(.width(24)) multiplexer_5 (
    .in0(register_file_1_busb), .in1(multiplexer_4_out), .out(multiplexer_5_out),
    .sel(control_unit_1_alusrc), .en(1'b1));
  RAM #(.addrWidth(24), .dataWidth(24), .bus("separate")) ram_1 (
    .addr(out_3), .din(register_file_1_busb), .data(ram_1_data), .str(control_unit_1_memwr), .sel(1'b1),
    .clk(clock_1_out), .ld(control_unit_1_memrd), .clr(in_2));
  Multiplexer #(.width(24)) multiplexer_6 (
    .in0(out_3), .in1(ram_1_data), .out(multiplexer_6_out), .sel(control_unit_1_wbdata), .en(1'b1));

  // Notes on the sheet:
  //   contents of rom_1 (hex, n*v repeats v):
  //   1a0018 9ad00 46c980 88eb00 9ad00 80e800 63b80 180027 16*0 104008 96800 98800 508804 ce000 17*0 a0500
  //   803b80
  //   Rs
  //   Rt
  //   Rd
endmodule

module ALU (
  input  [23:0] In_1,
  input  Shift_CAS,
  input  [23:0] In_2,
  input  [1:0] ALU_OP,
  input  SF,
  input  CMP,
  output [23:0] Output,
  output EQ,
  output Zero_Flag,
  output GT
);

  wire adder_1_cout, and_1_out, and_2_out, and_4_out, and_5_out, and_6_out, and_7_out, and_9_out, nand_1_out,
       or_1_out, or_2_out, or_3_out;
  wire [23:0] adder_1_out, and_3_out, bit_extender_1_out, multiplexer_1_out, multiplexer_2_out,
       multiplexer_3_out, shifter_1_out, xor_1_out;

  and and_1 (and_1_out, ALU_OP[0], ~ALU_OP[1]);  // AND_Gate
  assign bit_extender_1_out = {{23{and_2_out}}, and_2_out};  // Bit_Extender bit_extender_1
  and and_2 (and_2_out, 1'b1, and_1_out);
  assign xor_1_out = In_2 ^ bit_extender_1_out;  // XOR_Gate xor_1, 24 bits wide
  assign and_3_out = In_1 & In_2;  // AND_Gate and_3, 24 bits wide
  Adder #(.width(24)) adder_1 (.a(In_1), .b(xor_1_out), .out(adder_1_out), .cin(and_2_out), .cout(adder_1_cout));
  or or_1 (or_1_out, ALU_OP[0], ALU_OP[1]);
  nand nand_1 (nand_1_out, ALU_OP[0], ALU_OP[1]);
  Shifter #(.width(24)) shifter_1 (.in(In_2), .\dist (5'b00100), .out(shifter_1_out));
  Multiplexer #(.width(24)) multiplexer_1 (.in0(In_2), .in1(In_1), .out(multiplexer_1_out), .sel(GT));  // open: en
  Multiplexer #(.width(24)) multiplexer_2 (
    .in0(and_3_out), .in1(adder_1_out), .out(multiplexer_2_out), .sel(or_1_out), .en(nand_1_out));
  and and_4 (and_4_out, In_2[23], ~In_1[23]);  // AND_Gate
  and and_5 (and_5_out, ~In_2[23], In_1[23]);  // AND_Gate
  Multiplexer #(.width(24)) multiplexer_3 (
    .in0(shifter_1_out), .in1(multiplexer_1_out), .out(multiplexer_3_out), .sel(and_2_out));  // open: en
  Multiplexer #(.width(24)) multiplexer_4 (
    .in0(multiplexer_2_out), .in1(multiplexer_3_out), .out(Output), .sel(Shift_CAS), .en(nand_1_out));
  nor nor_1 (EQ, adder_1_out[23], adder_1_out[22], adder_1_out[21], adder_1_out[20], adder_1_out[19], adder_1_out[18], adder_1_out[17], adder_1_out[16], adder_1_out[15], adder_1_out[14], adder_1_out[13], adder_1_out[12], adder_1_out[11], adder_1_out[10], adder_1_out[9], adder_1_out[8], adder_1_out[7], adder_1_out[6], adder_1_out[5], adder_1_out[4], adder_1_out[3], adder_1_out[2], adder_1_out[1], adder_1_out[0]);
  and and_6 (and_6_out, adder_1_cout, ~EQ);  // AND_Gate
  or or_2 (or_2_out, and_6_out, and_4_out);
  and and_7 (and_7_out, EQ, SF);
  and and_8 (GT, or_2_out, ~and_5_out, ALU_OP[0], ~ALU_OP[1]);  // AND_Gate
  and and_9 (and_9_out, ~EQ, ~GT, CMP, ~ALU_OP[0], ALU_OP[1]);  // AND_Gate
  or or_3 (or_3_out, and_7_out, and_9_out);
  and and_10 (Zero_Flag, or_3_out, nand_1_out);

  // Notes on the sheet:
  //   00 AND
  //   /SHIFT
  //   /CAS
  //   01 SUB
  //   10 ADD
  //   11 don't care
  //   When C_OUT != 0, and ZF == 0 ==> GT  OR If first input was +ve and the second is -ve
endmodule

module Control_Unit (
  input  EQ,
  input  CLK,
  input  ZF,
  input  [23:0] Instruction,
  output CMP,
  output ALUSrc2,
  output [1:0] RegDst,
  output WriteSel,
  output [1:0] PC_OP,
  output ALUSrc,
  output [1:0] ALU_Op,
  output TypeSel,
  output MemWr,
  output MemRd,
  output RegWr,
  output WBData,
  output SF,
  output SHL
);

  wire and_1_out, and_2_out, and_3_out, d_ff_1_q, decoder_1_out0, decoder_1_out1, decoder_1_out2,
       decoder_1_out3, decoder_1_out4, decoder_1_out6, decoder_1_out7, decoder_1_out8, decoder_1_out9,
       decoder_1_out10, decoder_1_out11, decoder_1_out12, nor_1_out, nor_2_out, nor_3_out, nor_4_out,
       or_1_out, or_2_out, or_3_out, or_5_out, or_6_out, or_7_out, or_9_out;

  D_Flip_Flop d_ff_1 (.clk(CLK), .D(ZF), .Q(d_ff_1_q));  // open: Qn, preset, en, reset
  Decoder #(.select(5)) decoder_1 (
    .out0(decoder_1_out0), .out1(decoder_1_out1), .out2(decoder_1_out2), .out3(decoder_1_out3),
    .out4(decoder_1_out4), .out5(CMP), .out6(decoder_1_out6), .out7(decoder_1_out7), .out8(decoder_1_out8),
    .out9(decoder_1_out9), .out10(decoder_1_out10), .out11(decoder_1_out11), .out12(decoder_1_out12),
    .out13(RegDst[0]), .out14(ALUSrc2), .sel(Instruction[21:17]));  // open: out15, out16, out17, out18, out19, out20, out21, out22, out23, out24, out25, out26, out27, out28, out29, out30, out31, en
  and and_1 (and_1_out, ~Instruction[22], Instruction[23], ~d_ff_1_q);  // AND_Gate
  and and_2 (and_2_out, Instruction[22], ~Instruction[23], d_ff_1_q);  // AND_Gate
  nor nor_1 (nor_1_out, Instruction[22], Instruction[23]);
  or or_1 (or_1_out, decoder_1_out12, RegDst[0]);
  and and_3 (and_3_out, decoder_1_out11, EQ);
  nor nor_2 (nor_2_out, and_1_out, and_2_out, nor_1_out);
  Priority_Encoder #(.select(2)) priority_encoder_1 (
    .in0(1'b1), .in1(and_3_out), .in2(or_1_out), .in3(decoder_1_out6), .out(PC_OP));  // open: gs, en_out, en_in
  or or_2 (or_2_out, ALUSrc2, or_3_out);
  or or_3 (or_3_out, decoder_1_out7, decoder_1_out8, decoder_1_out9);
  or or_4 (ALUSrc, or_2_out, decoder_1_out10);
  or or_5 (or_5_out, decoder_1_out0, decoder_1_out7);
  or or_6 (or_6_out, decoder_1_out1, decoder_1_out4, CMP, decoder_1_out11);
  or or_7 (or_7_out, decoder_1_out2, decoder_1_out3, decoder_1_out8, decoder_1_out9, decoder_1_out10);
  or or_8 (WBData, decoder_1_out9, decoder_1_out2);
  nor nor_3 (nor_3_out, CMP, decoder_1_out6, decoder_1_out10, decoder_1_out11, decoder_1_out12);
  nor nor_4 (nor_4_out, decoder_1_out12, RegDst[0], ALUSrc2);
  and and_4 (SF, nor_4_out, Instruction[16]);
  or or_9 (or_9_out, ALUSrc2, RegDst[0], or_5_out);
  or or_10 (TypeSel, decoder_1_out6, ALUSrc, decoder_1_out11);
  or or_11 (SHL, ALUSrc2, decoder_1_out1);
  Priority_Encoder #(.select(2)) priority_encoder_2 (
    .in0(or_9_out), .in1(or_6_out), .in2(or_7_out), .in3(nor_2_out), .out(ALU_Op));  // open: gs, en_out, en_in
  and and_5 (MemWr, decoder_1_out10, ~nor_2_out);  // AND_Gate
  and and_6 (MemRd, WBData, ~nor_2_out);  // AND_Gate
  and and_7 (RegWr, nor_3_out, ~nor_2_out);  // AND_Gate

  assign RegDst[1] = ALUSrc2;
  assign WriteSel = RegDst[0];

  // Notes on the sheet:
  //   SF
  //   COND
  //   OPCODE
  //   NE
  //   EQ
  //   Normal
  //   If Any Expansion Occurs to Datapath, this should be changed to OR gate with 9 inputs
endmodule
